# Fritzing sketch schematic (saved by Fritzing 1.0.2b)

parts:
  SmartDriveDuo10A1 = MDDS10
  Mod1 = Raspberry Pi 4B
  DC_Mot_Enc1 = DC Motor with two-phase hall-encoder [part_number=VT-E-G25A-06-177E]
  DC_Mot_Enc2 = DC Motor with two-phase hall-encoder [part_number=VT-E-G25A-06-177E]
  BAT1 = 12 battery [package=battery]
  M1 = RioRand LM2596

nets:
  N1: SmartDriveDuo10A1.no_name_yet#connector_AN1, Mod1.GPIO13
  N2: SmartDriveDuo10A1.no_name_yet#connector_AN2, Mod1.GPIO12
  N3: SmartDriveDuo10A1.no_name_yet#connector_B1, BAT1.+, M1.Pin_1
  N4: SmartDriveDuo10A1.no_name_yet#connector_B2, BAT1.-, M1.Pin_2
  N5: SmartDriveDuo10A1.no_name_yet#connector_DIG1, Mod1.GPIO19
  N6: SmartDriveDuo10A1.no_name_yet#connector_DIG2, Mod1.GPIO16
  N7: SmartDriveDuo10A1.no_name_yet#connector_GND0, Mod1.GND, M1.Pin_4
  N8: SmartDriveDuo10A1.no_name_yet#connector_MLA1, DC_Mot_Enc1.pin6
  N9: SmartDriveDuo10A1.no_name_yet#connector_MLB1, DC_Mot_Enc1.pin1
  N10: SmartDriveDuo10A1.no_name_yet#connector_MRA1, DC_Mot_Enc2.pin1
  N11: SmartDriveDuo10A1.no_name_yet#connector_MRB1, DC_Mot_Enc2.pin6
  N12: Mod1.5V, M1.Pin_3

custom parts:
  12 battery: 12V lead acid type battery, like the Husqvarna YTH2448 12V 35AH battery. This is the mini version 1/4 the size of the actual battery to be closer to typical breadboard parts (around 2in wide rathher than 7in). The pads in pcb are sized to accomidate up to 14ga wire (as these batterys will deliver high currents.)
