# Fritzing sketch schematic_v2 (saved by Fritzing 1.0.4)
breadboards: 1

parts:
  SmartDriveDuo10A1 = MDDS10
  Mod1 = Raspberry Pi 4B
  DC_Mot_Enc1 = DC Motor with two-phase hall-encoder [part_number=VT-E-G25A-06-177E]
  DC_Mot_Enc2 = DC Motor with two-phase hall-encoder [part_number=VT-E-G25A-06-177E]
  J1 = Camdenboss CTB0158-3 [part_number=CTB0158-3 package=THT]
  J2 = Camdenboss CTB0158-2 [part_number=CTB0158-2 package=THT]
  J3 = Camdenboss CTB0158-3 [part_number=CTB0158-3 package=THT]
  J4 = Camdenboss CTB0158-2 [part_number=CTB0158-2 package=THT]
  J5 = Camdenboss CTB0158-2 [part_number=CTB0158-2 package=THT]
  J6 = Camdenboss CTB0158-2 [part_number=CTB0158-2 package=THT]
  J7 = Camdenboss CTB0158-2 [part_number=CTB0158-2 package=THT]
  J8 = Camdenboss CTB0158-2 [part_number=CTB0158-2 package=THT]
  J10 = Wago 221-412
  J11 = Wago 221-412
  J12 = Wago 221-412
  U4 = SWITCH-SPST-2 [package=switch-spst-vertical]
  U5 = SWITCH-SPST-2 [package=switch-spst-vertical]
  U6 = DC 5V TO ± 12V Mini DC converter [package=THT]
  J13 = Wago 221-412
  U3 = LIPO-2000mAh [package=lipo-2000]

nets:
  N1: SmartDriveDuo10A1.no_name_yet#connector_AN1, Mod1.GPIO13
  N2: SmartDriveDuo10A1.no_name_yet#connector_AN2, Mod1.GPIO12
  N3: SmartDriveDuo10A1.no_name_yet#connector_B1, J1.terminal_1
  N4: SmartDriveDuo10A1.no_name_yet#connector_B2, J3.terminal_3
  N5: SmartDriveDuo10A1.no_name_yet#connector_DIG1, Mod1.GPIO19
  N6: SmartDriveDuo10A1.no_name_yet#connector_DIG2, Mod1.GPIO16
  N7: SmartDriveDuo10A1.no_name_yet#connector_GND0, Mod1.GND, J4.terminal_1
  N8: SmartDriveDuo10A1.no_name_yet#connector_MLA1, J7.terminal_2
  N9: SmartDriveDuo10A1.no_name_yet#connector_MLB1, J8.terminal_1
  N10: SmartDriveDuo10A1.no_name_yet#connector_MRA1, J6.terminal_2
  N11: Mod1.5V, J5.terminal_1
  N12: DC_Mot_Enc1.pin1, J8.terminal_2
  N13: DC_Mot_Enc1.pin6, J7.terminal_1
  N14: DC_Mot_Enc2.pin1, J6.terminal_1
  N15: DC_Mot_Enc2.pin6, J2.terminal_2
  N16: J1.pin1, J1.pin2, J1.pin3
  N17: J1.terminal_2, U6.Vin
  N18: J1.terminal_3, J10.Pin_1, J10.Pin_2, U4.O
  N19: J2.pin1, J2.pin2
  N20: J3.pin1, J3.pin2, J3.pin3
  N21: J3.terminal_1, U5.O, J13.Pin_1, J13.Pin_2
  N22: J3.terminal_2, U6.GND
  N23: J4.pin1, J4.pin2
  N24: J4.terminal_2, U6.+12V
  N25: J5.pin1, J5.pin2
  N26: J5.terminal_2, U6.-12V
  N27: J6.pin1, J6.pin2
  N28: J7.pin1, J7.pin2
  N29: J8.pin1, J8.pin2
  N30: J11.Pin_1, J11.Pin_2, U4.P, U3.+
  N31: J12.Pin_1, J12.Pin_2, U5.P, U3.-

custom parts:
  Wago 221-412: Wago 221-412 2 position splicing connector 12AWG.
  DC 5V TO ± 12V Mini DC converter: DC 5V TO ± 12V Mini DC converter from ebay (search for "DC 5V TO ± 12V Mini DC converter"). Supplies ± 12V at up to 30MA output for op amps or rs232 drivers from a 3 to 5V input (so a battery or 3.3 or 5V power rail) on a micro).
